// Logisim project UAL.circ as structural Verilog: 1 circuit, main circuit main
module main (
  input  [7:0] Rs,
  input  [7:0] Rt,
  input  [2:0] ctrUAL,
  output CF,
  output ZF,
  output OF,
  output SF,
  output [7:0] RO
);

  Adder adder_1 ();  // open: a, b, out, cin, cout
  Subtractor subtractor_1 ();  // open: a, b, out, bin, bout
  // OR_Gate or_1 is placed but not wired
  // AND_Gate and_1 is placed but not wired
endmodule
